# Fritzing sketch AnalogWrite_LED_P8_13 (saved by Fritzing 0.8.3b)
breadboards: 1

parts:
  BeagleBone1 = BeagleBone Black
  LED1 = LED - 5mm [color="Red (633nm)" package="5 mm [THT]"]

nets:
  N1: BeagleBone1.no_name_yet#1, LED1.cathode
  N2: BeagleBone1.no_name_yet#113, LED1.anode

custom parts:
  BeagleBone Black: BeagleBone Black rev. A5B
